# Fritzing sketch pcb (saved by Fritzing 0.9.2b)

parts:
  RGBLed = RGB LED - (4 legs) [package="5 mm [THT]"]
  R1 = Resistor [resistance=330 tolerance=±5% package=THT]
  R2 = Resistor [resistance=330 tolerance=±5% package=THT]
  R3 = Resistor [resistance=330 tolerance=±5% package=THT]
  PIR = PIR sensor
  ArduinoMega5v = Arduino Mega 2560 (Rev3)
  5v = Power Jack [package=power_jack_pth]
  R4 = Resistor [tolerance=±5% resistance=10k package="1206 [SMD]"]

nets:
  N1: RGBLed.red_cathode, R1.Pin_0
  VCC: RGBLed.common_anode, PIR.VCC, ArduinoMega5v.5V, 5v.PWR, R4.Pin_0
  N2: RGBLed.green_cathode, R2.Pin_0
  N3: RGBLed.blue_cathode, R3.Pin_0
  N4: R1.Pin_1, ArduinoMega5v.D6_PWM
  N5: R2.Pin_1, ArduinoMega5v.D5_PWM
  N6: R3.Pin_1, ArduinoMega5v.D4_PWM
  GND: PIR.GND, ArduinoMega5v.GND, 5v.GNDBREAK
  N7: PIR.SIG, ArduinoMega5v.D14/TX3, R4.Pin_1
